// Logisim project Encryption.circ as structural Verilog: 2 circuits, main circuit main
module main (
  input  [6:0] in_1,
  input  [6:0] in_2,
  output [6:0] out_3
);

  wire [2:0] logical_left_bit_shifter_1_out_2;
  wire [6:0] not_1_out;

  not not_1 (not_1_out[0], in_1[0]);
  not not_2 (not_1_out[2], in_1[2]);
  not not_3 (not_1_out[4], in_1[4]);
  not not_4 (not_1_out[6], in_1[6]);
  assign out_3 = in_2 ^ {not_1_out[6], logical_left_bit_shifter_1_out_2[2], not_1_out[4], logical_left_bit_shifter_1_out_2[1], not_1_out[2], logical_left_bit_shifter_1_out_2[0], not_1_out[0]};  // XOR_Gate xor_1, 7 bits wide
  Logical_Left_Bit_shifter logical_left_bit_shifter_1 (
    .in_1({in_1[5], in_1[3], in_1[1]}), .out_2(logical_left_bit_shifter_1_out_2));

  // Notes on the sheet:
  //   INPUT 7 BIT ASCII
  //   PRIVATE KEY INPUT
  //   COMMENTS
  //   BIT SHIFTER
  //   Working: 1) Even bits are inverted    2)Odd bits are combined and shifted left     3) The intermediate message is the XORed with private key
  //   <-
  //   |
  //   INTERMEDIATE ENCRYTED MESSAGE
  //   FINAL ENCRYPTED MESSAGE OUTPUT
endmodule

module Logical_Left_Bit_shifter (
  input  [2:0] in_1,
  output [2:0] out_2
);


  assign out_2 = {in_1[0], in_1[2:1]};
endmodule
