// Logisim project InputOutput.circ as structural Verilog: 1 circuit, main circuit main
module main (
);

  wire clock_1_out, clock_2_out, controlled_buffer_1_out, controlled_buffer_2_out, keyboard_1_avail,
       keyboard_2_avail;
  wire [6:0] keyboard_1_data, keyboard_2_data;

  TTY tty_1 (.data(keyboard_1_data), .clk(clock_1_out));  // open: we, clr
  Clock clock_1 (.out(clock_1_out));
  assign controlled_buffer_1_out = keyboard_1_avail ? clock_1_out : 1'bz;  // Controlled_Buffer controlled_buffer_1
  Keyboard keyboard_1 (
    .clk(controlled_buffer_1_out), .avail(keyboard_1_avail), .data(keyboard_1_data));  // open: re, clr
  TTY tty_2 (.data(keyboard_2_data), .clk(clock_1_out));  // open: we, clr
  TTY tty_3 (.data(keyboard_2_data), .clk(clock_2_out));  // open: we, clr
  Clock clock_2 (.out(clock_2_out));
  assign controlled_buffer_2_out = keyboard_2_avail ? clock_2_out : 1'bz;  // Controlled_Buffer controlled_buffer_2
  Keyboard keyboard_2 (
    .clk(controlled_buffer_2_out), .avail(keyboard_2_avail), .data(keyboard_2_data));  // open: re, clr
  TTY tty_4 (.data(keyboard_1_data), .clk(clock_2_out));  // open: we, clr

  // Notes on the sheet:
  //   OUTGOING MESSAGE MONITOR A
  //   KEYBOARD A
  //   INCOMING MESSAGE MONITOR A
  //   MESSAGE SENDING MODULE HERE
  //   OUTGOING MESSAGE MONITOR B
  //   KEYBOARD B
  //   INCOMING MESSAGE MONITOR B
endmodule
